# Fritzing sketch Tiny85 Programmer (saved by Fritzing 0.9.3b)
circuit board: 8.74397cm x 1.25809cm
breadboards: 1

parts:
  U1 = SO16 [chip_label=CH340G package=SO]
  XTAL2 = Crystal [frequency="16 MHz" package=THT]
  C1 = Ceramic Capacitor [capacitance=10µF package="0805 [SMD, multilayer]"]
  C2 = Ceramic Capacitor [capacitance=0.47µF package="0805 [SMD, multilayer]"]
  C3 = Ceramic Capacitor [capacitance=1nF package="0805 [SMD, multilayer]"]
  C5 = Ceramic Capacitor [capacitance=22pF package="0805 [SMD, multilayer]"]
  C4 = Ceramic Capacitor [capacitance=22pF package="0805 [SMD, multilayer]"]
  X1 = USB Connectors [package=usb-a-pcb]
  R1 = Resistor [tolerance=±1% resistance=10 package="0805 [SMD]"]
  R3 = Resistor [tolerance=±1% resistance=1k package="0805 [SMD]"]
  R2 = Resistor [tolerance=±1% resistance=1k package="0805 [SMD]"]
  L2 = smd LED [color="Green (555nm)" package="0805 [SMD]"]
  L1 = smd LED [color="Green (555nm)" package="0805 [SMD]"]
  U2 = IC, DIP package, 16 pins [chip_label=ZIF]
  J1 = double row female pin header, 6 pins [form="♀ (female)"]
  F = Resettable Fuse PTC [package=ptc-1206]

nets:
  GND: U1.1, C1.1, C2.1, C3.0, C5.0, C4.0, X1.GND, U2.pin4, J1.pin1
  N1: U1.2, L1.cathode, U2.pin1, J1.pin4
  N2: U1.3, L2.cathode, J1.pin5
  N3: U1.4, C3.1
  N4: U1.5, X1.D+
  N5: U1.6, X1.D-
  N6: U1.7, XTAL2.pin_1, C4.1
  N7: U1.8, XTAL2.pin_0, C5.1
  N8: U1.9, U2.pin14, J1.pin2
  N9: U1.13, U2.pin13, J1.pin6
  N10: U1.14, U2.pin15
  N11: U1.16, C2.0, R1.Pin_1
  5v: C1.0, R1.Pin_0, R3.Pin_0, R2.Pin_0, U2.pin16, J1.pin3, F.2
  N12: X1.VBUS, F.1
  N13: R3.Pin_1, L2.anode
  N14: R2.Pin_1, L1.anode

notes:
  GND
  CTS
  VCC
  TX
  RX
  DTR
